# Fritzing sketch PIRRGBLedProMini12V (saved by Fritzing 0.9.2b)

parts:
  RGBLed5v = RGB LED - (4 legs) [package="5 mm [THT]"]
  R1 = Resistor [resistance=330 tolerance=±5% package=THT]
  R2 = Resistor [resistance=330 tolerance=±5% package=THT]
  R3 = Resistor [resistance=330 tolerance=±5% package=THT]
  PIR = PIR sensor
  R4 = Resistor [resistance=10k tolerance=±5% package=THT]
  ArduinoProMini5v = Arduino Pro Mini v13
  BarrelJack12v = Power Jack [package=power_jack_pth]

nets:
  N1: RGBLed5v.red_cathode, R1.Pin_0
  VCC: RGBLed5v.common_anode, PIR.VCC, R4.Pin_1, ArduinoProMini5v.VCC
  N2: RGBLed5v.green_cathode, R2.Pin_0
  N3: RGBLed5v.blue_cathode, R3.Pin_0
  N4: R1.Pin_1, ArduinoProMini5v.D3_PWM
  N5: R2.Pin_1, ArduinoProMini5v.D5_PWM
  N6: R3.Pin_1, ArduinoProMini5v.D6_PWM
  GND: PIR.GND, ArduinoProMini5v.GND, BarrelJack12v.GND
  N7: PIR.SIG, R4.Pin_0, ArduinoProMini5v.D2
  N8: ArduinoProMini5v.RAW, BarrelJack12v.PWR
